// Logisim project 实验3.circ as structural Verilog: 18 circuits, main circuit 倒计时
module \倒计时  (
  input  ReSet
);

  wire clock_1_out, comparator_1_eq;
  wire [3:0] multiplexer_1_out, subtractor_1_out, \四位寄存器_1_out_5 ;

  Subtractor #(.width(4)) subtractor_1 (.a(\四位寄存器_1_out_5 ), .b(4'b0001), .out(subtractor_1_out));  // open: bin, bout
  Comparator #(.width(4)) comparator_1 (.a(4'b0000), .b(\四位寄存器_1_out_5 ), .eq(comparator_1_eq));  // open: gt, lt
  Multiplexer #(.width(4), .enable("false")) multiplexer_1 (
    .in0(subtractor_1_out), .in1(4'b1001), .out(multiplexer_1_out), .sel(comparator_1_eq));
  Clock clock_1 (.out(clock_1_out));
  \四位寄存器  \u_四位寄存器_1  (.in_3(multiplexer_1_out), .out_5(\四位寄存器_1_out_5 ), .CLK(clock_1_out), .ReSet(ReSet), .en(1'b1));
  Hex_Digit_Display hex_digit_display_1 (.value(\四位寄存器_1_out_5 ));  // open: dp

  // Notes on the sheet:
  //   倒计时
endmodule

// SR
module \SR锁存器  (
  input  ReSet,
  input  Set,
  output Q,
  output NOT_Q
);

  nor nor_1 (Q, ReSet, NOT_Q);
  nor nor_2 (NOT_Q, Q, Set);

  // Notes on the sheet:
  //   SR锁存器
endmodule

// D锁存
module \D锁存器  (
  input  CLK,
  input  D,
  output out_3,
  output out_4
);

  wire and_1_out, and_2_out, not_1_out;

  not not_1 (not_1_out, D);
  and and_1 (and_1_out, not_1_out, CLK);
  and and_2 (and_2_out, CLK, D);
  \SR锁存器  \sr锁存器_1  (.ReSet(and_1_out), .Set(and_2_out), .Q(out_3), .NOT_Q(out_4));

  // Notes on the sheet:
  //   D锁存
endmodule

// D触发
module \D触发器  (
  input  CLK,
  input  D,
  output Q
);

  wire \d锁存器_1_out_3 , not_1_out;

  not not_1 (not_1_out, CLK);
  \D锁存器  \d锁存器_1  (.D(D), .out_3(\d锁存器_1_out_3 ), .CLK(not_1_out));  // open: out_4
  \D锁存器  \d锁存器_2  (.D(\d锁存器_1_out_3 ), .out_3(Q), .CLK(CLK));  // open: out_4

  // Notes on the sheet:
  //   D触发器
endmodule

module \复位功能D触发器  (
  input  CLK,
  input  D,
  input  ReSet,
  output Q
);

  wire and_1_out, not_1_out;

  and and_1 (and_1_out, D, not_1_out);
  not not_1 (not_1_out, ReSet);
  \D触发器  \d触发器_1  (.D(and_1_out), .Q(Q), .CLK(CLK));

  // Notes on the sheet:
  //   复位功能的D触发器
endmodule

// D
module \复位_使能  (
  input  CKL,
  input  D,
  input  ReSet,
  input  en,
  output Q
);

  wire multiplexer_1_out;

  Multiplexer #(.enable("false")) multiplexer_1 (.in0(Q), .in1(D), .out(multiplexer_1_out), .sel(en));
  \复位功能D触发器  \u_复位功能d触发器_1  (.D(multiplexer_1_out), .Q(Q), .CLK(CKL), .ReSet(ReSet));

  // Notes on the sheet:
  //   带复位和使能的D触发器
endmodule

// 寄存器
module \四位寄存器  (
  input  CLK,
  input  en,
  input  [3:0] in_3,
  input  ReSet,
  output [3:0] out_5
);

  \复位_使能  \u_复位_使能_1  (.D(in_3[3]), .Q(out_5[3]), .CKL(CLK), .ReSet(ReSet), .en(en));
  \复位_使能  \u_复位_使能_2  (.D(in_3[2]), .Q(out_5[2]), .CKL(CLK), .ReSet(ReSet), .en(en));
  \复位_使能  \u_复位_使能_3  (.D(in_3[1]), .Q(out_5[1]), .CKL(CLK), .ReSet(ReSet), .en(en));
  \复位_使能  \u_复位_使能_4  (.D(in_3[0]), .Q(out_5[0]), .CKL(CLK), .ReSet(ReSet), .en(en));

  // Notes on the sheet:
  //   四位寄存器
endmodule

module \_4_3存储阵列  (
  input  [2:0] \输入总线 ,
  input  [1:0] \地址 ,
  input  ReSet,
  output [2:0] out_4
);

  wire clock_1_out, \复位_使能_1_q , \复位_使能_2_q , \复位_使能_3_q , \复位_使能_4_q , \复位_使能_5_q , \复位_使能_6_q ,
       \复位_使能_7_q , \复位_使能_8_q , \复位_使能_9_q , \复位_使能_10_q , \复位_使能_11_q , \复位_使能_12_q , \译码器_1_out_2 ,
       \译码器_1_out_3 , \译码器_1_out_4 , \译码器_1_out_5 ;

  \译码器  \u_译码器_1  (
    .in_1(\地址 ), .out_2(\译码器_1_out_2 ), .out_3(\译码器_1_out_3 ), .out_4(\译码器_1_out_4 ), .out_5(\译码器_1_out_5 ));
  \复位_使能  \u_复位_使能_1  (.D(\输入总线 [2]), .Q(\复位_使能_1_q ), .CKL(clock_1_out), .ReSet(ReSet), .en(\译码器_1_out_2 ));
  assign out_4[2] = \译码器_1_out_2  ? \复位_使能_1_q  : 1'bz;  // Controlled_Buffer controlled_buffer_1
  assign out_4[2] = \译码器_1_out_3  ? \复位_使能_2_q  : 1'bz;  // Controlled_Buffer controlled_buffer_2
  \复位_使能  \u_复位_使能_2  (.D(\输入总线 [2]), .Q(\复位_使能_2_q ), .CKL(clock_1_out), .ReSet(ReSet), .en(\译码器_1_out_3 ));
  \复位_使能  \u_复位_使能_3  (.D(\输入总线 [2]), .Q(\复位_使能_3_q ), .CKL(clock_1_out), .ReSet(ReSet), .en(\译码器_1_out_4 ));
  assign out_4[2] = \译码器_1_out_4  ? \复位_使能_3_q  : 1'bz;  // Controlled_Buffer controlled_buffer_3
  assign out_4[2] = \译码器_1_out_5  ? \复位_使能_4_q  : 1'bz;  // Controlled_Buffer controlled_buffer_4
  \复位_使能  \u_复位_使能_4  (.D(\输入总线 [2]), .Q(\复位_使能_4_q ), .CKL(clock_1_out), .ReSet(ReSet), .en(\译码器_1_out_5 ));
  \复位_使能  \u_复位_使能_5  (.D(\输入总线 [1]), .Q(\复位_使能_5_q ), .CKL(clock_1_out), .ReSet(ReSet), .en(\译码器_1_out_2 ));
  \复位_使能  \u_复位_使能_6  (.D(\输入总线 [1]), .Q(\复位_使能_6_q ), .CKL(clock_1_out), .ReSet(ReSet), .en(\译码器_1_out_3 ));
  \复位_使能  \u_复位_使能_7  (.D(\输入总线 [1]), .Q(\复位_使能_7_q ), .CKL(clock_1_out), .ReSet(ReSet), .en(\译码器_1_out_4 ));
  \复位_使能  \u_复位_使能_8  (.D(\输入总线 [1]), .Q(\复位_使能_8_q ), .CKL(clock_1_out), .ReSet(ReSet), .en(\译码器_1_out_5 ));
  assign out_4[1] = \译码器_1_out_2  ? \复位_使能_5_q  : 1'bz;  // Controlled_Buffer controlled_buffer_5
  assign out_4[1] = \译码器_1_out_3  ? \复位_使能_6_q  : 1'bz;  // Controlled_Buffer controlled_buffer_6
  assign out_4[1] = \译码器_1_out_4  ? \复位_使能_7_q  : 1'bz;  // Controlled_Buffer controlled_buffer_7
  assign out_4[1] = \译码器_1_out_5  ? \复位_使能_8_q  : 1'bz;  // Controlled_Buffer controlled_buffer_8
  assign out_4[0] = \译码器_1_out_2  ? \复位_使能_9_q  : 1'bz;  // Controlled_Buffer controlled_buffer_9
  \复位_使能  \u_复位_使能_9  (.D(\输入总线 [0]), .Q(\复位_使能_9_q ), .CKL(clock_1_out), .ReSet(ReSet), .en(\译码器_1_out_2 ));
  assign out_4[0] = \译码器_1_out_3  ? \复位_使能_10_q  : 1'bz;  // Controlled_Buffer controlled_buffer_10
  \复位_使能  \u_复位_使能_10  (.D(\输入总线 [0]), .Q(\复位_使能_10_q ), .CKL(clock_1_out), .ReSet(ReSet), .en(\译码器_1_out_3 ));
  assign out_4[0] = \译码器_1_out_4  ? \复位_使能_11_q  : 1'bz;  // Controlled_Buffer controlled_buffer_11
  \复位_使能  \u_复位_使能_11  (.D(\输入总线 [0]), .Q(\复位_使能_11_q ), .CKL(clock_1_out), .ReSet(ReSet), .en(\译码器_1_out_4 ));
  assign out_4[0] = \译码器_1_out_5  ? \复位_使能_12_q  : 1'bz;  // Controlled_Buffer controlled_buffer_12
  \复位_使能  \u_复位_使能_12  (.D(\输入总线 [0]), .Q(\复位_使能_12_q ), .CKL(clock_1_out), .ReSet(ReSet), .en(\译码器_1_out_5 ));
  Clock clock_1 (.out(clock_1_out));
endmodule

module \译码器  (
  input  [1:0] in_1,
  output out_2,
  output out_3,
  output out_4,
  output out_5
);

  wire not_1_out, not_2_out, not_3_out, not_4_out;

  and and_1 (out_2, in_1[0], in_1[1]);
  not not_1 (not_1_out, in_1[0]);
  and and_2 (out_3, not_1_out, in_1[1]);
  and and_3 (out_4, in_1[0], not_2_out);
  not not_2 (not_2_out, in_1[1]);
  not not_3 (not_3_out, in_1[0]);
  and and_4 (out_5, not_3_out, not_4_out);
  not not_4 (not_4_out, in_1[1]);

  // Notes on the sheet:
  //   译码器
endmodule

module \三态输出D触发器  (
  input  CLK,
  input  D,
  input  ReSet,
  input  en,
  output out_5
);

  wire \复位_使能_1_q ;

  \复位_使能  \u_复位_使能_1  (.D(D), .Q(\复位_使能_1_q ), .CKL(CLK), .ReSet(ReSet), .en(en));
  assign out_5 = en ? \复位_使能_1_q  : 1'bz;  // Controlled_Buffer controlled_buffer_1

  // Notes on the sheet:
  //   三态输出D触发器
endmodule

module \_4_3存储器阵列2  (
  input  [2:0] in_1,
  input  [1:0] in_2,
  input  in_3,
  output [2:0] out_4
);

  wire clock_1_out, \译码器_1_out_2 , \译码器_1_out_3 , \译码器_1_out_4 , \译码器_1_out_5 ;

  \译码器  \u_译码器_1  (
    .in_1(in_2), .out_2(\译码器_1_out_2 ), .out_3(\译码器_1_out_3 ), .out_4(\译码器_1_out_4 ), .out_5(\译码器_1_out_5 ));
  \三态输出D触发器  \u_三态输出d触发器_1  (.D(in_1[2]), .ReSet(in_3), .CLK(clock_1_out), .en(\译码器_1_out_2 ), .out_5(out_4[2]));
  \三态输出D触发器  \u_三态输出d触发器_2  (.D(in_1[2]), .ReSet(in_3), .CLK(clock_1_out), .en(\译码器_1_out_3 ), .out_5(out_4[2]));
  \三态输出D触发器  \u_三态输出d触发器_3  (.D(in_1[2]), .ReSet(in_3), .CLK(clock_1_out), .en(\译码器_1_out_4 ), .out_5(out_4[2]));
  \三态输出D触发器  \u_三态输出d触发器_4  (.D(in_1[2]), .ReSet(in_3), .CLK(clock_1_out), .en(\译码器_1_out_5 ), .out_5(out_4[2]));
  \三态输出D触发器  \u_三态输出d触发器_5  (.D(in_1[1]), .ReSet(in_3), .CLK(clock_1_out), .en(\译码器_1_out_2 ), .out_5(out_4[1]));
  \三态输出D触发器  \u_三态输出d触发器_6  (.D(in_1[1]), .ReSet(in_3), .CLK(clock_1_out), .en(\译码器_1_out_3 ), .out_5(out_4[1]));
  \三态输出D触发器  \u_三态输出d触发器_7  (.D(in_1[1]), .ReSet(in_3), .CLK(clock_1_out), .en(\译码器_1_out_4 ), .out_5(out_4[1]));
  \三态输出D触发器  \u_三态输出d触发器_8  (.D(in_1[1]), .ReSet(in_3), .CLK(clock_1_out), .en(\译码器_1_out_5 ), .out_5(out_4[1]));
  \三态输出D触发器  \u_三态输出d触发器_9  (.D(in_1[0]), .ReSet(in_3), .CLK(clock_1_out), .en(\译码器_1_out_2 ), .out_5(out_4[0]));
  \三态输出D触发器  \u_三态输出d触发器_10  (.D(in_1[0]), .ReSet(in_3), .CLK(clock_1_out), .en(\译码器_1_out_3 ), .out_5(out_4[0]));
  \三态输出D触发器  \u_三态输出d触发器_11  (.D(in_1[0]), .ReSet(in_3), .CLK(clock_1_out), .en(\译码器_1_out_4 ), .out_5(out_4[0]));
  \三态输出D触发器  \u_三态输出d触发器_12  (.D(in_1[0]), .ReSet(in_3), .CLK(clock_1_out), .en(\译码器_1_out_5 ), .out_5(out_4[0]));
  Clock clock_1 (.out(clock_1_out));
endmodule

module \四位移位寄存器  (
  input  CLK,
  input  \一位输入 ,
  input  ReSet,
  output \最后一位输出 ,
  output [3:0] \四位输出 
);

  \复位功能D触发器  \u_复位功能d触发器_1  (.D(\一位输入 ), .Q(\四位输出 [0]), .CLK(CLK), .ReSet(ReSet));
  \复位功能D触发器  \u_复位功能d触发器_2  (.D(\四位输出 [0]), .Q(\四位输出 [1]), .CLK(CLK), .ReSet(ReSet));
  \复位功能D触发器  \u_复位功能d触发器_3  (.D(\四位输出 [1]), .Q(\四位输出 [2]), .CLK(CLK), .ReSet(ReSet));
  \复位功能D触发器  \u_复位功能d触发器_4  (.D(\四位输出 [2]), .Q(\四位输出 [3]), .CLK(CLK), .ReSet(ReSet));

  assign \最后一位输出  = \四位输出 [3];

  // Notes on the sheet:
  //   四位移位寄存器
endmodule

module \跑马灯  (
  input  \模式选择 ,
  input  Start,
  input  \是否闪烁 ,
  input  ReSet
);

  wire [7:0] \模式选择_1_out_5 , \模式选择_1_out_6 , \模式选择_1_out_7 , \模式选择_1_out_8 , \模式选择_1_out_9 , \模式选择_1_out_10 ,
       \模式选择_1_out_11 , \模式选择_1_out_12 ;

  \模式选择  \u_模式选择_1  (
    .Start(Start), .out_5(\模式选择_1_out_5 ), .out_6(\模式选择_1_out_6 ), .out_7(\模式选择_1_out_7 ),
    .out_8(\模式选择_1_out_8 ), .out_9(\模式选择_1_out_9 ), .out_10(\模式选择_1_out_10 ), .out_11(\模式选择_1_out_11 ),
    .out_12(\模式选择_1_out_12 ), .\闪烁 (\是否闪烁 ), .ReSet(ReSet), .\模式选择 (\模式选择 ));
  LED led_1 (.in(\模式选择_1_out_5 [1]));
  LED led_2 (.in(\模式选择_1_out_5 [0]));
  LED led_3 (.in(\模式选择_1_out_6 [1]));
  LED led_4 (.in(\模式选择_1_out_6 [0]));
  LED led_5 (.in(\模式选择_1_out_7 [1]));
  LED led_6 (.in(\模式选择_1_out_7 [0]));
  LED led_7 (.in(\模式选择_1_out_8 [0]));
  LED led_8 (.in(\模式选择_1_out_8 [1]));
  LED led_9 (.in(\模式选择_1_out_9 [0]));
  LED led_10 (.in(\模式选择_1_out_9 [1]));
  LED led_11 (.in(\模式选择_1_out_10 [1]));
  LED led_12 (.in(\模式选择_1_out_10 [0]));
  LED led_13 (.in(\模式选择_1_out_11 [0]));
  LED led_14 (.in(\模式选择_1_out_11 [1]));
  LED led_15 (.in(\模式选择_1_out_12 [0]));
  LED led_16 (.in(\模式选择_1_out_12 [1]));
  LED led_17 (.in(\模式选择_1_out_5 [3]));
  LED led_18 (.in(\模式选择_1_out_5 [2]));
  LED led_19 (.in(\模式选择_1_out_6 [3]));
  LED led_20 (.in(\模式选择_1_out_6 [2]));
  LED led_21 (.in(\模式选择_1_out_7 [2]));
  LED led_22 (.in(\模式选择_1_out_7 [3]));
  LED led_23 (.in(\模式选择_1_out_8 [3]));
  LED led_24 (.in(\模式选择_1_out_8 [2]));
  LED led_25 (.in(\模式选择_1_out_9 [2]));
  LED led_26 (.in(\模式选择_1_out_9 [3]));
  LED led_27 (.in(\模式选择_1_out_10 [3]));
  LED led_28 (.in(\模式选择_1_out_10 [2]));
  LED led_29 (.in(\模式选择_1_out_11 [3]));
  LED led_30 (.in(\模式选择_1_out_11 [2]));
  LED led_31 (.in(\模式选择_1_out_12 [2]));
  LED led_32 (.in(\模式选择_1_out_12 [3]));
  LED led_33 (.in(\模式选择_1_out_5 [5]));
  LED led_34 (.in(\模式选择_1_out_5 [4]));
  LED led_35 (.in(\模式选择_1_out_6 [4]));
  LED led_36 (.in(\模式选择_1_out_6 [5]));
  LED led_37 (.in(\模式选择_1_out_7 [4]));
  LED led_38 (.in(\模式选择_1_out_7 [5]));
  LED led_39 (.in(\模式选择_1_out_8 [4]));
  LED led_40 (.in(\模式选择_1_out_8 [5]));
  LED led_41 (.in(\模式选择_1_out_9 [4]));
  LED led_42 (.in(\模式选择_1_out_9 [5]));
  LED led_43 (.in(\模式选择_1_out_10 [5]));
  LED led_44 (.in(\模式选择_1_out_10 [4]));
  LED led_45 (.in(\模式选择_1_out_11 [4]));
  LED led_46 (.in(\模式选择_1_out_11 [5]));
  LED led_47 (.in(\模式选择_1_out_12 [4]));
  LED led_48 (.in(\模式选择_1_out_12 [5]));
  LED led_49 (.in(\模式选择_1_out_5 [6]));
  LED led_50 (.in(\模式选择_1_out_5 [7]));
  LED led_51 (.in(\模式选择_1_out_6 [7]));
  LED led_52 (.in(\模式选择_1_out_6 [6]));
  LED led_53 (.in(\模式选择_1_out_7 [6]));
  LED led_54 (.in(\模式选择_1_out_7 [7]));
  LED led_55 (.in(\模式选择_1_out_8 [7]));
  LED led_56 (.in(\模式选择_1_out_8 [6]));
  LED led_57 (.in(\模式选择_1_out_9 [7]));
  LED led_58 (.in(\模式选择_1_out_9 [6]));
  LED led_59 (.in(\模式选择_1_out_10 [6]));
  LED led_60 (.in(\模式选择_1_out_10 [7]));
  LED led_61 (.in(\模式选择_1_out_11 [6]));
  LED led_62 (.in(\模式选择_1_out_11 [7]));
  LED led_63 (.in(\模式选择_1_out_12 [6]));
  LED led_64 (.in(\模式选择_1_out_12 [7]));

  // Notes on the sheet:
  //   跑马灯
endmodule

module \模式选择  (
  input  \模式选择 ,
  input  Start,
  input  ReSet,
  input  \闪烁 ,
  output [7:0] out_5,
  output [7:0] out_6,
  output [7:0] out_7,
  output [7:0] out_8,
  output [7:0] out_9,
  output [7:0] out_10,
  output [7:0] out_11,
  output [7:0] out_12
);

  wire and_1_out, and_2_out, clock_1_out, multiplexer_1_out, not_1_out, not_2_out;
  wire [15:0] \n64位移位寄存器_1_out_4 , \n64位移位寄存器_1_out_5 , \n64位移位寄存器_1_out_6 , \n64位移位寄存器_1_out_8 ;

  and and_1 (and_1_out, Start, \闪烁 );
  and and_2 (and_2_out, \闪烁 , not_1_out);
  not not_1 (not_1_out, out_12[7]);
  Clock clock_1 (.out(clock_1_out));
  Multiplexer #(.enable("false")) multiplexer_1 (
    .in0(Start), .in1(and_2_out), .out(multiplexer_1_out), .sel(and_1_out));
  not not_2 (not_2_out, \模式选择 );
  \_64位移位寄存器  \u_64位移位寄存器_1  (
    .in_2(multiplexer_1_out), .in_1(clock_1_out), .out_4(\n64位移位寄存器_1_out_4 ), .out_5(\n64位移位寄存器_1_out_5 ),
    .out_6(\n64位移位寄存器_1_out_6 ), .out_8(\n64位移位寄存器_1_out_8 ), .ReSet(ReSet));  // open: out_7
  \第一种模式  \u_第一种模式_1  (
    .en(not_2_out), .in_2(\n64位移位寄存器_1_out_4 ), .in_3(\n64位移位寄存器_1_out_5 ), .in_4(\n64位移位寄存器_1_out_6 ),
    .in_5(\n64位移位寄存器_1_out_8 ), .out_6(out_5), .out_7(out_6), .out_8(out_7), .out_9(out_8), .out_10(out_9),
    .out_11(out_10), .out_12(out_11), .out_13(out_12));
  \第二种模式  \u_第二种模式_1  (
    .en(\模式选择 ), .in_2(\n64位移位寄存器_1_out_4 ), .in_3(\n64位移位寄存器_1_out_5 ), .in_4(\n64位移位寄存器_1_out_6 ),
    .in_5(\n64位移位寄存器_1_out_8 ), ._1(out_5), ._3(out_7), ._8(out_12), ._4(out_8), ._2(out_6), ._5(out_9),
    ._6(out_10), ._7(out_11));

  // Notes on the sheet:
  //   寄存器及模式选择
endmodule

module \倒置  (
  input  [7:0] in_1,
  output [7:0] out_2
);


  assign out_2 = {in_1[0], in_1[1], in_1[2], in_1[3], in_1[4], in_1[5], in_1[6], in_1[7]};
endmodule

module \_64位移位寄存器  (
  input  in_1,
  input  in_2,
  input  ReSet,
  output [15:0] out_4,
  output [15:0] out_5,
  output [15:0] out_6,
  output out_7,
  output [15:0] out_8
);

  wire \四位移位寄存器_1_最后一位输出 , \四位移位寄存器_2_最后一位输出 , \四位移位寄存器_3_最后一位输出 , \四位移位寄存器_4_最后一位输出 , \四位移位寄存器_5_最后一位输出 ,
       \四位移位寄存器_6_最后一位输出 , \四位移位寄存器_7_最后一位输出 , \四位移位寄存器_8_最后一位输出 , \四位移位寄存器_9_最后一位输出 , \四位移位寄存器_10_最后一位输出 ,
       \四位移位寄存器_11_最后一位输出 , \四位移位寄存器_12_最后一位输出 , \四位移位寄存器_13_最后一位输出 , \四位移位寄存器_14_最后一位输出 ,
       \四位移位寄存器_15_最后一位输出 ;

  \四位移位寄存器  \u_四位移位寄存器_1  (
    .\一位输入 (in_2), .\最后一位输出 (\四位移位寄存器_1_最后一位输出 ), .\四位输出 (out_4[3:0]), .CLK(in_1), .ReSet(ReSet));
  \四位移位寄存器  \u_四位移位寄存器_2  (
    .\一位输入 (\四位移位寄存器_10_最后一位输出 ), .\最后一位输出 (\四位移位寄存器_2_最后一位输出 ), .\四位输出 (out_5[3:0]), .CLK(in_1),
    .ReSet(ReSet));
  \四位移位寄存器  \u_四位移位寄存器_3  (
    .\一位输入 (\四位移位寄存器_11_最后一位输出 ), .\最后一位输出 (\四位移位寄存器_3_最后一位输出 ), .\四位输出 (out_6[3:0]), .CLK(in_1),
    .ReSet(ReSet));
  \四位移位寄存器  \u_四位移位寄存器_4  (
    .\一位输入 (\四位移位寄存器_1_最后一位输出 ), .\最后一位输出 (\四位移位寄存器_4_最后一位输出 ), .\四位输出 (out_4[7:4]), .CLK(in_1), .ReSet(ReSet));
  \四位移位寄存器  \u_四位移位寄存器_5  (
    .\一位输入 (\四位移位寄存器_2_最后一位输出 ), .\最后一位输出 (\四位移位寄存器_5_最后一位输出 ), .\四位输出 (out_5[7:4]), .CLK(in_1), .ReSet(ReSet));
  \四位移位寄存器  \u_四位移位寄存器_6  (
    .\一位输入 (\四位移位寄存器_3_最后一位输出 ), .\最后一位输出 (\四位移位寄存器_6_最后一位输出 ), .\四位输出 (out_6[7:4]), .CLK(in_1), .ReSet(ReSet));
  \四位移位寄存器  \u_四位移位寄存器_7  (
    .\一位输入 (\四位移位寄存器_8_最后一位输出 ), .\最后一位输出 (\四位移位寄存器_7_最后一位输出 ), .\四位输出 (out_8[7:4]), .CLK(in_1), .ReSet(ReSet));
  \四位移位寄存器  \u_四位移位寄存器_8  (
    .\一位输入 (\四位移位寄存器_14_最后一位输出 ), .\最后一位输出 (\四位移位寄存器_8_最后一位输出 ), .\四位输出 (out_8[3:0]), .CLK(in_1),
    .ReSet(ReSet));
  \四位移位寄存器  \u_四位移位寄存器_9  (
    .\一位输入 (\四位移位寄存器_4_最后一位输出 ), .\最后一位输出 (\四位移位寄存器_9_最后一位输出 ), .\四位输出 (out_4[11:8]), .CLK(in_1),
    .ReSet(ReSet));
  \四位移位寄存器  \u_四位移位寄存器_10  (
    .\一位输入 (\四位移位寄存器_9_最后一位输出 ), .\最后一位输出 (\四位移位寄存器_10_最后一位输出 ), .\四位输出 (out_4[15:12]), .CLK(in_1),
    .ReSet(ReSet));
  \四位移位寄存器  \u_四位移位寄存器_11  (
    .\一位输入 (\四位移位寄存器_12_最后一位输出 ), .\最后一位输出 (\四位移位寄存器_11_最后一位输出 ), .\四位输出 (out_5[15:12]), .CLK(in_1),
    .ReSet(ReSet));
  \四位移位寄存器  \u_四位移位寄存器_12  (
    .\一位输入 (\四位移位寄存器_5_最后一位输出 ), .\最后一位输出 (\四位移位寄存器_12_最后一位输出 ), .\四位输出 (out_5[11:8]), .CLK(in_1),
    .ReSet(ReSet));
  \四位移位寄存器  \u_四位移位寄存器_13  (
    .\一位输入 (\四位移位寄存器_6_最后一位输出 ), .\最后一位输出 (\四位移位寄存器_13_最后一位输出 ), .\四位输出 (out_6[11:8]), .CLK(in_1),
    .ReSet(ReSet));
  \四位移位寄存器  \u_四位移位寄存器_14  (
    .\一位输入 (\四位移位寄存器_13_最后一位输出 ), .\最后一位输出 (\四位移位寄存器_14_最后一位输出 ), .\四位输出 (out_6[15:12]), .CLK(in_1),
    .ReSet(ReSet));
  \四位移位寄存器  \u_四位移位寄存器_15  (
    .\一位输入 (\四位移位寄存器_7_最后一位输出 ), .\最后一位输出 (\四位移位寄存器_15_最后一位输出 ), .\四位输出 (out_8[11:8]), .CLK(in_1),
    .ReSet(ReSet));
  \四位移位寄存器  \u_四位移位寄存器_16  (
    .\一位输入 (\四位移位寄存器_15_最后一位输出 ), .\最后一位输出 (out_7), .\四位输出 (out_8[15:12]), .CLK(in_1), .ReSet(ReSet));

  // Notes on the sheet:
  //   六十四位移位寄存器（串联）
endmodule

// 模式一
module \第一种模式  (
  input  en,
  input  [15:0] in_2,
  input  [15:0] in_3,
  input  [15:0] in_4,
  input  [15:0] in_5,
  output [7:0] out_6,
  output [7:0] out_7,
  output [7:0] out_8,
  output [7:0] out_9,
  output [7:0] out_10,
  output [7:0] out_11,
  output [7:0] out_12,
  output [7:0] out_13
);

  wire [15:8] controlled_buffer_1_out, controlled_buffer_2_out, controlled_buffer_3_out,
       controlled_buffer_4_out;

  assign {controlled_buffer_1_out, out_6} = en ? in_2 : 16'bz;  // Controlled_Buffer controlled_buffer_1
  assign {controlled_buffer_2_out, out_8} = en ? in_3 : 16'bz;  // Controlled_Buffer controlled_buffer_2
  assign {controlled_buffer_3_out, out_10} = en ? in_4 : 16'bz;  // Controlled_Buffer controlled_buffer_3
  assign {controlled_buffer_4_out, out_12} = en ? in_5 : 16'bz;  // Controlled_Buffer controlled_buffer_4
  \倒置  \u_倒置_1  (.in_1(controlled_buffer_1_out), .out_2(out_7));
  \倒置  \u_倒置_2  (.in_1(controlled_buffer_2_out), .out_2(out_9));
  \倒置  \u_倒置_3  (.in_1(controlled_buffer_3_out), .out_2(out_11));
  \倒置  \u_倒置_4  (.in_1(controlled_buffer_4_out), .out_2(out_13));

  // Notes on the sheet:
  //   模式一
endmodule

// 模式二
module \第二种模式  (
  input  en,
  input  [15:0] in_2,
  input  [15:0] in_3,
  input  [15:0] in_4,
  input  [15:0] in_5,
  output [7:0] _1,
  output [7:0] _8,
  output [7:0] _2,
  output [7:0] _7,
  output [7:0] _3,
  output [7:0] _6,
  output [7:0] _4,
  output [7:0] _5
);

  assign {_5[3], _5[4], _4[4:2], _5[2], _6[2], _6[3], _6[4], _6[5], _5[5], _4[5], _3[5:2]} = en ? in_5 : 16'bz;  // Controlled_Buffer controlled_buffer_1
  assign {_8[6], _8[7], _7[7], _6[7], _5[7], _4[7], _3[7], _2[7], _1} = en ? in_2 : 16'bz;  // Controlled_Buffer controlled_buffer_2
  assign {_2[4:0], _3[0], _4[0], _5[0], _6[0], _7[0], _8[0], _8[1], _8[2], _8[3], _8[4], _8[5]} = en ? in_3 : 16'bz;  // Controlled_Buffer controlled_buffer_3
  assign {_3[1], _4[1], _5[1], _6[1], _7[1], _7[2], _7[3], _7[4], _7[5], _7[6], _6[6], _5[6], _4[6], _3[6], _2[6:5]} = en ? in_4 : 16'bz;  // Controlled_Buffer controlled_buffer_4

  // Notes on the sheet:
  //   模式二
  //   4.6
endmodule
