// Logisim project 实验一.circ as structural Verilog: 5 circuits, main circuit main
module main (
  input  A1,
  input  A0,
  input  B1,
  input  B0,
  input  B1_2,
  input  A1_2,
  input  B0_2,
  input  A0_2,
  input  in_9,
  input  shamt,
  input  A1_3,
  input  B1_3,
  input  A0_3,
  input  B0_3,
  output out_15,
  output S1,
  output S0,
  output S,
  output out_19,
  output out_20,
  output out_21,
  output S1_2,
  output S0_2
);

  wire \n2_1复用器2bit_1_b0_2 , \n2_1复用器2bit_1_b1_2 , not_1_out, not_2_out, not_3_out, not_4_out, \全加器_3_cout ,
       \全加器_4_cout , \全加器_6_cout ;

  \全加器  \u_全加器_1  (.Cin(\全加器_3_cout ), .A(B1_2), .B(A1_2), .Cout(out_15), .S(S1));
  \全加器  \u_全加器_2  (.Cin(\全加器_4_cout ), .A(A1_3), .B(not_1_out), .Cout(out_19), .S(S1_2));
  not not_1 (not_1_out, B1_3);
  \全加器  \u_全加器_3  (.Cin(in_9), .A(B0_2), .B(A0_2), .Cout(\全加器_3_cout ), .S(S0));
  not not_2 (not_2_out, B0_3);
  \全加器  \u_全加器_4  (.Cin(1'b1), .A(A0_3), .B(not_2_out), .Cout(\全加器_4_cout ), .S(S0_2));
  \全加器  \u_全加器_5  (.Cin(\全加器_6_cout ), .A(A1), .B(\n2_1复用器2bit_1_b1_2 ), .Cout(S), .S(out_20));
  not not_3 (not_3_out, B0);
  not not_4 (not_4_out, B1);
  \_2_1复用器2bit  \u_2_1复用器2bit_1  (
    .Shamt(shamt), .NOTB1(not_4_out), .B1(B1), .NOTB0(not_3_out), .B0(B0), .B1_2(\n2_1复用器2bit_1_b1_2 ),
    .B0_2(\n2_1复用器2bit_1_b0_2 ));
  \全加器  \u_全加器_6  (.Cin(shamt), .A(A0), .B(\n2_1复用器2bit_1_b0_2 ), .Cout(\全加器_6_cout ), .S(out_21));

  // Notes on the sheet:
  //   二位加法
  //   二位减法
  //   2bit2：1复用器
endmodule

// full adder
module \全加器  (
  input  Cin,
  input  A,
  input  B,
  output Cout,
  output S
);

  wire and_1_out, and_2_out, and_3_out, or_1_out, xor_1_out;

  and and_1 (and_1_out, B, A);
  and and_2 (and_2_out, B, Cin);
  and and_3 (and_3_out, A, Cin);
  or or_1 (or_1_out, and_1_out, and_2_out);
  xor xor_1 (xor_1_out, Cin, A);
  or or_2 (Cout, or_1_out, and_3_out);
  xor xor_2 (S, xor_1_out, B);
endmodule

module \_2_1复用器  (
  input  NOTB1,
  input  B1,
  input  NOTB0,
  input  B0,
  input  shamt,
  output SB0,
  output SB0_2
);

  wire and_1_out, and_2_out, and_3_out, and_4_out, not_1_out, not_2_out;

  not not_1 (not_1_out, shamt);
  and and_1 (and_1_out, NOTB1, shamt);
  and and_2 (and_2_out, B1, not_1_out);
  or or_1 (SB0_2, and_1_out, and_2_out);
  and and_3 (and_3_out, NOTB0, shamt);
  and and_4 (and_4_out, B0, not_2_out);
  or or_2 (SB0, and_3_out, and_4_out);
  not not_2 (not_2_out, shamt);
endmodule

// 2：1
module \_2_1复用器2bit  (
  input  NOTB1,
  input  B1,
  input  NOTB0,
  input  B0,
  input  Shamt,
  output B1_2,
  output B0_2
);

  \_2_1复用器1bit  \u_2_1复用器1bit_1  (.B1(NOTB1), .B0(B1), .out_4(B1_2), .Shamt(Shamt));
  \_2_1复用器1bit  \u_2_1复用器1bit_2  (.B1(NOTB0), .B0(B0), .out_4(B0_2), .Shamt(Shamt));

  // Notes on the sheet:
  //   2：1复用器2bit
endmodule

// 1bit
module \_2_1复用器1bit  (
  input  B1,
  input  B0,
  input  Shamt,
  output out_4
);

  wire and_1_out, and_2_out, not_1_out;

  and and_1 (and_1_out, B1, Shamt);
  not not_1 (not_1_out, Shamt);
  and and_2 (and_2_out, B0, not_1_out);
  or or_1 (out_4, and_1_out, and_2_out);

  // Notes on the sheet:
  //   2：1复用器1bit
endmodule
