// Logisim project 有限状态机.circ as structural Verilog: 18 circuits, main circuit 红绿灯系统
module \红绿灯系统  (
  input  TA,
  input  TB,
  input  ReSet
);

  wire clock_1_out, d_ff_1_q, d_ff_2_q, \状态转换_1_s11 , \状态转换_1_s22 , \输出红绿灯_1_la_green , \输出红绿灯_1_la_red ,
       \输出红绿灯_1_la_yellow , \输出红绿灯_1_lb_green , \输出红绿灯_1_lb_red , \输出红绿灯_1_lb_yellow ;

  Clock clock_1 (.out(clock_1_out));
  \状态转换  \u_状态转换_1  (.S1(d_ff_1_q), .S0(d_ff_2_q), .TA(TA), .TB(TB), .S11(\状态转换_1_s11 ), .S22(\状态转换_1_s22 ));
  D_Flip_Flop d_ff_1 (.clk(clock_1_out), .D(\状态转换_1_s11 ), .Q(d_ff_1_q), .reset(ReSet));  // open: Qn, preset, en
  D_Flip_Flop d_ff_2 (.clk(clock_1_out), .D(\状态转换_1_s22 ), .Q(d_ff_2_q), .reset(ReSet));  // open: Qn, preset, en
  \输出红绿灯  \u_输出红绿灯_1  (
    .S1(d_ff_1_q), .S0(d_ff_2_q), .LA_Green(\输出红绿灯_1_la_green ), .LA_Yellow(\输出红绿灯_1_la_yellow ),
    .LA_Red(\输出红绿灯_1_la_red ), .LB_Green(\输出红绿灯_1_lb_green ), .LB_Yellow(\输出红绿灯_1_lb_yellow ),
    .LB_Red(\输出红绿灯_1_lb_red ));
  LED LA_Green (.in(\输出红绿灯_1_la_green ));
  LED LA_Yellow (.in(\输出红绿灯_1_la_yellow ));
  LED LA_Red (.in(\输出红绿灯_1_la_red ));
  LED LB_Green (.in(\输出红绿灯_1_lb_green ));
  LED LB_Yellow (.in(\输出红绿灯_1_lb_yellow ));
  LED LB_Red (.in(\输出红绿灯_1_lb_red ));
endmodule

module \状态转换  (
  input  S1,
  input  S0,
  input  TA,
  input  TB,
  output S11,
  output S22
);

  wire and_1_out, and_2_out, and_3_out, and_4_out, not_1_out, not_2_out, not_3_out, not_4_out, not_5_out,
       not_6_out, not_7_out;

  not not_1 (not_1_out, S1);
  and and_1 (and_1_out, not_1_out, S0);
  and and_2 (and_2_out, S1, not_2_out);
  not not_2 (not_2_out, S0);
  not not_3 (not_3_out, S1);
  and and_3 (and_3_out, not_3_out, not_4_out, not_5_out);
  not not_4 (not_4_out, S0);
  not not_5 (not_5_out, TA);
  and and_4 (and_4_out, S1, not_6_out, not_7_out);
  not not_6 (not_6_out, S0);
  not not_7 (not_7_out, TB);
  or or_1 (S11, and_1_out, and_2_out);
  or or_2 (S22, and_3_out, and_4_out);

  // Notes on the sheet:
  //   状态转化
endmodule

module \输出红绿灯  (
  input  S1,
  input  S0,
  output LA_Green,
  output LA_Yellow,
  output LA_Red,
  output LB_Green,
  output LB_Yellow,
  output LB_Red
);

  wire not_1_out, not_2_out, not_3_out, not_4_out;

  not not_1 (not_1_out, S1);
  not not_2 (not_2_out, S0);
  not not_3 (not_3_out, S1);
  not not_4 (not_4_out, S0);
  and and_1 (LB_Yellow, S1, S0);
  not not_5 (LB_Red, S1);
  and and_2 (LA_Green, not_1_out, not_2_out);
  and and_3 (LA_Yellow, not_3_out, S0);
  and and_4 (LB_Green, S1, not_4_out);

  assign LA_Red = S1;

  // Notes on the sheet:
  //   输出红绿灯
endmodule

module \电子锁  (
  input  in_1,
  output LOCK
);

  wire button_1_out, d_ff_1_q, d_ff_2_q, \电子锁状态转换_1_s11 , \电子锁状态转换_1_s22 ;

  Button button_1 (.out(button_1_out));
  \电子锁状态转换  \u_电子锁状态转换_1  (.S2(d_ff_1_q), .S1(d_ff_2_q), .D(in_1), .S22(\电子锁状态转换_1_s22 ), .S11(\电子锁状态转换_1_s11 ));
  D_Flip_Flop d_ff_1 (.clk(button_1_out), .D(\电子锁状态转换_1_s22 ), .Q(d_ff_1_q));  // open: Qn, preset, en, reset
  D_Flip_Flop d_ff_2 (.clk(button_1_out), .D(\电子锁状态转换_1_s11 ), .Q(d_ff_2_q));  // open: Qn, preset, en, reset
  \电子锁输出  \u_电子锁输出_1  (.S2(d_ff_1_q), .S1(d_ff_2_q), .LOCK(LOCK));

  // Notes on the sheet:
  //   S2
  //   S1
endmodule

module \电子锁状态转换  (
  input  S2,
  input  S1,
  input  D,
  output S22,
  output S11
);


  assign S11 = D;
  assign S22 = S1;

  // Notes on the sheet:
  //   状态转化
endmodule

module \电子锁输出  (
  input  S2,
  input  S1,
  output LOCK
);

  wire not_1_out;

  not not_1 (not_1_out, S2);
  and and_1 (LOCK, not_1_out, S1);

  // Notes on the sheet:
  //   开锁
endmodule

module \长按_短按  (
  input  ReSet
);

  wire button_1_out, CLK_out, d_ff_1_q, d_ff_2_q, d_ff_3_q, \长短按状态转化_1_s0_next , \长短按状态转化_1_s1_next ,
       \长短按状态转化_1_s2_next , \长短按输出_1_dl , \长短按输出_1_ds ;

  Button button_1 (.out(button_1_out));
  Clock CLK (.out(CLK_out));
  \长短按状态转化  \u_长短按状态转化_1  (
    .s2(d_ff_1_q), .s1(d_ff_2_q), .s0(d_ff_3_q), .d(button_1_out), .s2_next(\长短按状态转化_1_s2_next ),
    .s1_next(\长短按状态转化_1_s1_next ), .s0_next(\长短按状态转化_1_s0_next ));
  D_Flip_Flop d_ff_1 (.clk(CLK_out), .D(\长短按状态转化_1_s2_next ), .Q(d_ff_1_q), .reset(ReSet));  // open: Qn, preset, en
  D_Flip_Flop d_ff_2 (.clk(CLK_out), .D(\长短按状态转化_1_s1_next ), .Q(d_ff_2_q), .reset(ReSet));  // open: Qn, preset, en
  D_Flip_Flop d_ff_3 (.clk(CLK_out), .D(\长短按状态转化_1_s0_next ), .Q(d_ff_3_q), .reset(ReSet));  // open: Qn, preset, en
  \长短按输出  \u_长短按输出_1  (.s2(d_ff_1_q), .s1(d_ff_2_q), .s0(d_ff_3_q), .DL(\长短按输出_1_dl ), .DS(\长短按输出_1_ds ));
  LED led_1 (.in(\长短按输出_1_dl ));
  LED led_2 (.in(\长短按输出_1_ds ));

  // Notes on the sheet:
  //   DL
  //   DS
endmodule

module \长短按状态转化  (
  input  s2,
  input  s1,
  input  s0,
  input  d,
  output s2_next,
  output s1_next,
  output s0_next
);


  assign s0_next = d;
  assign s1_next = s0;
  assign s2_next = s1;

  // Notes on the sheet:
  //   状态转化
endmodule

module \长短按输出  (
  input  s2,
  input  s1,
  input  s0,
  output DL,
  output DS
);

  wire not_1_out, not_2_out, not_3_out;

  not not_1 (not_1_out, s0);
  not not_2 (not_2_out, s2);
  not not_3 (not_3_out, s0);
  and and_1 (DL, s2, s1, not_1_out);
  and and_2 (DS, not_2_out, s1, not_3_out);

  // Notes on the sheet:
  //   DS，DL输出
endmodule

module \台灯亮度  (
  input  ReSet
);

  wire button_1_out, CLK_out, d_ff_1_q, d_ff_2_q, d_ff_3_q, d_ff_4_q, d_ff_5_q, d_ff_6_q, d_ff_7_q,
       \亮度输出_1_l0 , \亮度输出_1_l1 , \亮度输出_1_l2 , \亮度输出_1_l3 , \台灯状态转化_1_s0_next , \台灯状态转化_1_s1_next ,
       \台灯状态转化_1_s2_next , \台灯状态转化_1_s3_next , \长短按状态转化_1_s0_next , \长短按状态转化_1_s1_next , \长短按状态转化_1_s2_next ;

  Button button_1 (.out(button_1_out));
  Clock CLK (.out(CLK_out));
  \台灯状态转化  \u_台灯状态转化_1  (
    .S3(d_ff_1_q), .S2(d_ff_2_q), .S1(d_ff_3_q), .S0(d_ff_4_q), .d2(d_ff_5_q), .d1(d_ff_6_q), .d0(d_ff_7_q),
    .S3_next(\台灯状态转化_1_s3_next ), .S2_next(\台灯状态转化_1_s2_next ), .S1_next(\台灯状态转化_1_s1_next ),
    .S0_next(\台灯状态转化_1_s0_next ));
  \长短按状态转化  \u_长短按状态转化_1  (
    .s2(d_ff_5_q), .s1(d_ff_6_q), .s0(d_ff_7_q), .d(button_1_out), .s2_next(\长短按状态转化_1_s2_next ),
    .s1_next(\长短按状态转化_1_s1_next ), .s0_next(\长短按状态转化_1_s0_next ));
  D_Flip_Flop d_ff_1 (.clk(CLK_out), .D(\台灯状态转化_1_s3_next ), .Q(d_ff_1_q), .reset(ReSet));  // open: Qn, preset, en
  D_Flip_Flop d_ff_2 (.clk(CLK_out), .D(\台灯状态转化_1_s2_next ), .Q(d_ff_2_q), .reset(ReSet));  // open: Qn, preset, en
  D_Flip_Flop d_ff_3 (.clk(CLK_out), .D(\台灯状态转化_1_s1_next ), .Q(d_ff_3_q));  // open: Qn, preset, en, reset
  D_Flip_Flop d_ff_4 (.clk(CLK_out), .D(\台灯状态转化_1_s0_next ), .Q(d_ff_4_q), .reset(ReSet));  // open: Qn, preset, en
  D_Flip_Flop d_ff_5 (.clk(CLK_out), .D(\长短按状态转化_1_s2_next ), .Q(d_ff_5_q), .reset(ReSet));  // open: Qn, preset, en
  D_Flip_Flop d_ff_6 (.clk(CLK_out), .D(\长短按状态转化_1_s1_next ), .Q(d_ff_6_q), .reset(ReSet));  // open: Qn, preset, en
  D_Flip_Flop d_ff_7 (.clk(CLK_out), .D(\长短按状态转化_1_s0_next ), .Q(d_ff_7_q), .reset(ReSet));  // open: Qn, preset, en
  \亮度输出  \u_亮度输出_1  (
    .S3(d_ff_1_q), .S2(d_ff_2_q), .S1(d_ff_3_q), .S0(d_ff_4_q), .L3(\亮度输出_1_l3 ), .L2(\亮度输出_1_l2 ),
    .L1(\亮度输出_1_l1 ), .L0(\亮度输出_1_l0 ));
  LED led_1 (.in(\亮度输出_1_l3 ));
  LED led_2 (.in(\亮度输出_1_l2 ));
  LED led_3 (.in(\亮度输出_1_l1 ));
  LED led_4 (.in(\亮度输出_1_l0 ));

  // Notes on the sheet:
  //   L3
  //   L2
  //   L1
  //   L0
endmodule

module \台灯状态转化  (
  input  S3,
  input  S2,
  input  S1,
  input  S0,
  input  d2,
  input  d1,
  input  d0,
  output S3_next,
  output S2_next,
  output S1_next,
  output S0_next
);

  wire and_1_out, and_2_out, and_3_out, and_4_out, and_5_out, and_6_out, and_7_out, and_8_out, and_9_out,
       and_10_out, and_11_out, and_12_out, and_13_out, and_14_out, and_15_out, and_16_out, and_17_out,
       and_18_out, and_19_out, and_20_out, and_21_out, and_22_out, and_23_out, and_24_out, and_25_out,
       not_1_out, not_2_out, not_3_out, not_4_out, not_5_out, not_6_out, not_7_out, not_8_out, not_9_out,
       not_10_out, not_11_out, not_12_out, not_13_out, not_14_out, not_15_out, not_16_out, not_17_out,
       not_18_out, not_19_out, not_20_out, not_21_out, not_22_out, not_23_out, not_24_out, not_25_out,
       not_26_out, not_27_out, not_28_out, not_29_out, not_30_out, not_31_out, not_32_out, not_33_out,
       not_34_out, not_35_out, not_36_out, not_37_out;

  not not_1 (not_1_out, S2);
  not not_2 (not_2_out, S1);
  not not_3 (not_3_out, S0);
  not not_4 (not_4_out, d2);
  not not_5 (not_5_out, d0);
  not not_6 (not_6_out, S1);
  not not_7 (not_7_out, d0);
  not not_8 (not_8_out, S3);
  not not_9 (not_9_out, d0);
  not not_10 (not_10_out, S3);
  not not_11 (not_11_out, d0);
  not not_12 (not_12_out, d1);
  not not_13 (not_13_out, d1);
  not not_14 (not_14_out, d2);
  not not_15 (not_15_out, d0);
  not not_16 (not_16_out, S3);
  not not_17 (not_17_out, S3);
  not not_18 (not_18_out, d2);
  not not_19 (not_19_out, S2);
  not not_20 (not_20_out, d2);
  not not_21 (not_21_out, S2);
  not not_22 (not_22_out, S0);
  not not_23 (not_23_out, S2);
  not not_24 (not_24_out, S1);
  not not_25 (not_25_out, S0);
  not not_26 (not_26_out, d2);
  not not_27 (not_27_out, d0);
  not not_28 (not_28_out, S3);
  not not_29 (not_29_out, d2);
  not not_30 (not_30_out, S0);
  not not_31 (not_31_out, d2);
  not not_32 (not_32_out, S3);
  not not_33 (not_33_out, d2);
  and and_1 (and_1_out, not_1_out, not_2_out, not_3_out, not_4_out, d1, not_5_out);
  and and_2 (and_2_out, not_6_out, S0, d2, d1, not_7_out);
  and and_3 (and_3_out, not_8_out, S1, d2, d1, not_9_out);
  and and_4 (and_4_out, not_10_out, S2, d2, d1, not_11_out);
  and and_5 (and_5_out, S3, not_34_out);
  not not_34 (not_34_out, d1);
  and and_6 (and_6_out, S3, d0);
  and and_7 (and_7_out, S2, not_12_out);
  and and_8 (and_8_out, S2, d2);
  and and_9 (and_9_out, S3, S1, S0, d2, d1, d0);
  and and_10 (and_10_out, S3, S2, d0);
  and and_11 (and_11_out, S1, not_13_out);
  and and_12 (and_12_out, S1, not_14_out, d0);
  and and_13 (and_13_out, S1, d2, not_15_out);
  and and_14 (and_14_out, not_16_out, S1, S0, d2);
  and and_15 (and_15_out, not_17_out, S2, not_18_out, d1, d0);
  and and_16 (and_16_out, S3, not_19_out, not_20_out, d1, d0);
  and and_17 (and_17_out, S3, not_21_out, not_22_out, d2);
  and and_18 (and_18_out, not_23_out, not_24_out, not_25_out, not_26_out, d1, not_27_out);
  and and_19 (and_19_out, S0, not_35_out);
  not not_35 (not_35_out, d1);
  and and_20 (and_20_out, not_28_out, S0, not_29_out, d0);
  not not_36 (not_36_out, S1);
  and and_21 (and_21_out, not_36_out, S0, d2);
  and and_22 (and_22_out, S0, d2, not_37_out);
  not not_37 (not_37_out, d0);
  and and_23 (and_23_out, S1, not_30_out, d2, d1, d0);
  and and_24 (and_24_out, S1, S0, not_31_out, d0);
  and and_25 (and_25_out, not_32_out, S2, not_33_out, d1, d0);
  or or_1 (S2_next, and_7_out, and_8_out, and_9_out, and_10_out);
  or or_2 (S1_next, and_11_out, and_12_out, and_13_out, and_14_out, and_15_out, and_16_out, and_17_out);
  or or_3 (S3_next, and_1_out, and_2_out, and_3_out, and_4_out, and_5_out, and_6_out);
  or or_4 (S0_next, and_18_out, and_19_out, and_20_out, and_21_out, and_22_out, and_23_out, and_24_out, and_25_out);
endmodule

module \亮度输出  (
  input  S3,
  input  S2,
  input  S1,
  input  S0,
  output L3,
  output L2,
  output L1,
  output L0
);

  wire and_1_out;

  and and_1 (and_1_out, S1, S0);
  or or_1 (L1, S1, S2);
  or or_2 (L0, S0, S1, S2);
  or or_3 (L2, and_1_out, S2);

  assign L3 = S2;

  // Notes on the sheet:
  //   输出
endmodule

module \弹球  (
  input  ReSet
);

  wire clock_1_out;
  wire [7:0] \显示_1_out_3 , \显示_1_out_4 , \显示_1_out_5 , \显示_1_out_6 , \显示_1_out_7 , \显示_1_out_8 ,
       \显示_1_out_9 , \显示_1_out_10 , \显示_1_out_11 , \显示_1_out_12 , \显示_1_out_13 , \显示_1_out_14 ,
       \显示_1_out_15 , \显示_1_out_16 , \显示_1_out_17 , \显示_1_out_18 , \移动_1_out_6 , \随机x_y生成_1_y ;
  wire [15:0] \移动_1_out_5 , \随机x_y生成_1_x ;

  Clock clock_1 (.out(clock_1_out));
  \随机x_y生成  \u_随机x_y生成_1  (.ReSet(ReSet), .X(\随机x_y生成_1_x ), .Y(\随机x_y生成_1_y ));
  DotMatrix #(.matrixcols(16), .matrixrows(8)) dotmatrix_1 (
    .col0(\显示_1_out_11 ), .col1(\显示_1_out_3 ), .col2(\显示_1_out_12 ), .col3(\显示_1_out_4 ),
    .col4(\显示_1_out_13 ), .col5(\显示_1_out_5 ), .col6(\显示_1_out_14 ), .col7(\显示_1_out_6 ),
    .col8(\显示_1_out_15 ), .col9(\显示_1_out_7 ), .col10(\显示_1_out_16 ), .col11(\显示_1_out_8 ),
    .col12(\显示_1_out_17 ), .col13(\显示_1_out_9 ), .col14(\显示_1_out_18 ), .col15(\显示_1_out_10 ));
  \显示  \u_显示_1  (
    .Y(\移动_1_out_6 ), .X(\移动_1_out_5 ), .out_11(\显示_1_out_11 ), .out_3(\显示_1_out_3 ), .out_12(\显示_1_out_12 ),
    .out_4(\显示_1_out_4 ), .out_13(\显示_1_out_13 ), .out_5(\显示_1_out_5 ), .out_14(\显示_1_out_14 ),
    .out_6(\显示_1_out_6 ), .out_15(\显示_1_out_15 ), .out_7(\显示_1_out_7 ), .out_16(\显示_1_out_16 ),
    .out_8(\显示_1_out_8 ), .out_17(\显示_1_out_17 ), .out_9(\显示_1_out_9 ), .out_18(\显示_1_out_18 ),
    .out_10(\显示_1_out_10 ));
  \移动  \u_移动_1  (
    .CLK(clock_1_out), .ReSet(ReSet), .X(\随机x_y生成_1_x ), .Y(\随机x_y生成_1_y ), .out_5(\移动_1_out_5 ),
    .out_6(\移动_1_out_6 ));
endmodule

// 随机
module \随机x_y生成  (
  input  ReSet,
  output [15:0] X,
  output [7:0] Y
);

  wire [2:0] random_2_out;
  wire [3:0] random_1_out;

  Random #(.width(4), .seed(100)) random_1 (.clk(ReSet), .out(random_1_out));  // open: next, clr
  Random #(.width(3), .seed(100)) random_2 (.clk(ReSet), .out(random_2_out));  // open: next, clr
  Shifter #(.width(16)) shifter_1 (.in(16'h1), .\dist (random_1_out), .out(X));
  Shifter shifter_2 (.in(8'h1), .\dist (random_2_out), .out(Y));
endmodule

module \显示  (
  input  [7:0] Y,
  input  [15:0] X,
  output [7:0] out_3,
  output [7:0] out_4,
  output [7:0] out_5,
  output [7:0] out_6,
  output [7:0] out_7,
  output [7:0] out_8,
  output [7:0] out_9,
  output [7:0] out_10,
  output [7:0] out_11,
  output [7:0] out_12,
  output [7:0] out_13,
  output [7:0] out_14,
  output [7:0] out_15,
  output [7:0] out_16,
  output [7:0] out_17,
  output [7:0] out_18
);

  Multiplexer #(.width(8), .enable("false")) multiplexer_1 (.in0({8{1'b0}}), .in1(Y), .out(out_11), .sel(X[0]));
  Multiplexer #(.width(8), .enable("false")) multiplexer_2 (.in0({8{1'b0}}), .in1(Y), .out(out_3), .sel(X[1]));
  Multiplexer #(.width(8), .enable("false")) multiplexer_3 (.in0({8{1'b0}}), .in1(Y), .out(out_12), .sel(X[2]));
  Multiplexer #(.width(8), .enable("false")) multiplexer_4 (.in0({8{1'b0}}), .in1(Y), .out(out_4), .sel(X[3]));
  Multiplexer #(.width(8), .enable("false")) multiplexer_5 (.in0({8{1'b0}}), .in1(Y), .out(out_13), .sel(X[4]));
  Multiplexer #(.width(8), .enable("false")) multiplexer_6 (.in0({8{1'b0}}), .in1(Y), .out(out_5), .sel(X[5]));
  Multiplexer #(.width(8), .enable("false")) multiplexer_7 (.in0({8{1'b0}}), .in1(Y), .out(out_14), .sel(X[6]));
  Multiplexer #(.width(8), .enable("false")) multiplexer_8 (.in0({8{1'b0}}), .in1(Y), .out(out_6), .sel(X[7]));
  Multiplexer #(.width(8), .enable("false")) multiplexer_9 (.in0({8{1'b0}}), .in1(Y), .out(out_15), .sel(X[8]));
  Multiplexer #(.width(8), .enable("false")) multiplexer_10 (.in0({8{1'b0}}), .in1(Y), .out(out_7), .sel(X[9]));
  Multiplexer #(.width(8), .enable("false")) multiplexer_11 (.in0({8{1'b0}}), .in1(Y), .out(out_8), .sel(X[11]));
  Multiplexer #(.width(8), .enable("false")) multiplexer_12 (.in0({8{1'b0}}), .in1(Y), .out(out_16), .sel(X[10]));
  Multiplexer #(.width(8), .enable("false")) multiplexer_13 (.in0({8{1'b0}}), .in1(Y), .out(out_17), .sel(X[12]));
  Multiplexer #(.width(8), .enable("false")) multiplexer_14 (.in0({8{1'b0}}), .in1(Y), .out(out_9), .sel(X[13]));
  Multiplexer #(.width(8), .enable("false")) multiplexer_15 (.in0({8{1'b0}}), .in1(Y), .out(out_10), .sel(X[15]));
  Multiplexer #(.width(8), .enable("false")) multiplexer_16 (.in0({8{1'b0}}), .in1(Y), .out(out_18), .sel(X[14]));
endmodule

module \移动  (
  input  CLK,
  input  ReSet,
  input  [15:0] X,
  input  [7:0] Y,
  output [15:0] out_5,
  output [7:0] out_6
);

  wire comparator_1_eq, comparator_2_eq, comparator_3_eq, comparator_4_eq, d_ff_1_q, d_ff_2_q,
       \x移动_1_q_next , \y移动_1_q_next ;
  wire [7:0] multiplexer_2_out, multiplexer_3_out, shifter_3_out, shifter_4_out;
  wire [15:0] multiplexer_1_out, multiplexer_4_out, shifter_1_out, shifter_2_out;

  Multiplexer #(.width(16), .enable("false")) multiplexer_1 (
    .in0(out_5), .in1(X), .out(multiplexer_1_out), .sel(ReSet));
  Multiplexer #(.width(8), .enable("false")) multiplexer_2 (.in0(out_6), .in1(Y), .out(multiplexer_2_out), .sel(ReSet));
  Comparator comparator_1 (.a(8'h40), .b(multiplexer_2_out), .eq(comparator_1_eq));  // open: gt, lt
  Comparator comparator_2 (.a(8'h2), .b(multiplexer_2_out), .eq(comparator_2_eq));  // open: gt, lt
  Comparator #(.width(16)) comparator_3 (.a(16'h4000), .b(multiplexer_1_out), .eq(comparator_3_eq));  // open: gt, lt
  \X移动  \x移动_1  (.Q(d_ff_1_q), .U(comparator_3_eq), .D(comparator_4_eq), .Q_next(\x移动_1_q_next ));
  Comparator #(.width(16)) comparator_4 (.a(16'h2), .b(multiplexer_1_out), .eq(comparator_4_eq));  // open: gt, lt
  \Y移动  \y移动_1  (.Q(d_ff_2_q), .L(comparator_1_eq), .R(comparator_2_eq), .Q_next(\y移动_1_q_next ));
  D_Flip_Flop d_ff_1 (.clk(CLK), .D(\x移动_1_q_next ), .Q(d_ff_1_q));  // open: Qn, preset, en, reset
  D_Flip_Flop d_ff_2 (.clk(CLK), .D(\y移动_1_q_next ), .Q(d_ff_2_q));  // open: Qn, preset, en, reset
  Shifter #(.width(16)) shifter_1 (.in(multiplexer_1_out), .\dist (4'b0001), .out(shifter_1_out));
  Shifter #(.width(16), .shift("lr")) shifter_2 (.in(multiplexer_1_out), .\dist (4'b0001), .out(shifter_2_out));
  Shifter shifter_3 (.in(multiplexer_2_out), .\dist (3'b001), .out(shifter_3_out));
  Shifter #(.shift("lr")) shifter_4 (.in(multiplexer_2_out), .\dist (3'b001), .out(shifter_4_out));
  Multiplexer #(.width(8), .enable("false")) multiplexer_3 (
    .in0(shifter_3_out), .in1(shifter_4_out), .out(multiplexer_3_out), .sel(d_ff_2_q));
  Multiplexer #(.width(16), .enable("false")) multiplexer_4 (
    .in0(shifter_1_out), .in1(shifter_2_out), .out(multiplexer_4_out), .sel(d_ff_1_q));
  Register #(.width(16)) register_1 (.D(multiplexer_4_out), .Q(out_5), .clk(CLK));  // open: en, clr
  Register register_2 (.D(multiplexer_3_out), .Q(out_6), .clk(CLK));  // open: en, clr

  // Notes on the sheet:
  //   0上
  //   1右移
  //   0左移
  //   1下
endmodule

module \Y移动  (
  input  Q,
  input  L,
  input  R,
  output Q_next
);

  wire and_1_out, and_2_out, and_3_out, not_1_out, not_2_out;

  not not_1 (not_1_out, R);
  not not_2 (not_2_out, R);
  and and_1 (and_1_out, L, not_1_out);
  and and_2 (and_2_out, Q, not_2_out);
  and and_3 (and_3_out, Q, L);
  or or_1 (Q_next, and_1_out, and_2_out, and_3_out);

  // Notes on the sheet:
  //   y状态变化
endmodule

module \X移动  (
  input  Q,
  input  U,
  input  D,
  output Q_next
);

  wire and_1_out, and_2_out, and_3_out, not_1_out, not_2_out;

  not not_1 (not_1_out, D);
  not not_2 (not_2_out, D);
  and and_1 (and_1_out, U, not_1_out);
  and and_2 (and_2_out, Q, not_2_out);
  and and_3 (and_3_out, Q, U);
  or or_1 (Q_next, and_1_out, and_2_out, and_3_out);

  // Notes on the sheet:
  //   x状态变化
endmodule
