// Logisim project 锁存器.circ as structural Verilog: 12 circuits, main circuit main
module main (
  input  CLK,
  input  CLK_2,
  input  D,
  input  D_2,
  input  CLK_3,
  input  EN,
  input  EN_2,
  input  ReSet,
  input  D_3,
  input  Set,
  input  CLK_4,
  input  D0,
  input  D1,
  input  D2,
  input  D3,
  input  CLK_5,
  input  CLK_6,
  input  CLK_7,
  input  A1,
  input  D_4,
  input  D3_2,
  input  D2_2,
  input  A0,
  input  D_5,
  input  D1_2,
  input  D0_2,
  input  RESET_2,
  output out_28,
  output out_29,
  output out_30,
  output Q,
  output out_32,
  output Q_2,
  output Q_3,
  output Not_Q,
  output Not_Q_2,
  output Q_4,
  output Q3,
  output Q_5,
  output Q2,
  output Q1,
  output Q0,
  output Q1_2,
  output Q2_2,
  output Q3_2,
  output Q0_2,
  output Not_Q_3
);

  wire not_3_out;

  not not_1 (out_28, out_30);
  not not_2 (out_30, out_28);
  \SR锁存器  \sr锁存器_1  (.ReSet(ReSet), .Set(Set), .Q(Q_2), .Not_Q(Not_Q));
  \D触发器  \d触发器_1  (.D(D_5), .out_3(Q_5), .out_4(Not_Q_3), .in_1(CLK_6));
  not not_3 (not_3_out, out_29);
  \D锁存器  \d锁存器_1  (.D(D_3), .Q(Q_3), .Not_Q(Not_Q_2), .CLK(CLK_3));
  \寄存器  \u_寄存器_1  (.D3(D3_2), .D2(D2_2), .D1(D1_2), .D0(D0_2), .Q3(Q3), .Q2(Q2), .Q1(Q1), .Q0(Q0_2), .in_1(CLK_7));
  not not_4 (out_29, not_3_out);
  \带使能端的D触发器  \u_带使能端的d触发器_1  (.D(D), .Q(Q), .EN(EN_2), .CLK(CLK));
  \带复位功能的触发器  \u_带复位功能的触发器_1  (.D(D_4), .Q(Q_4), .CLK(CLK_4), .in_3(RESET_2));
  \带使能端的复用器2  \u_带使能端的复用器2_1  (.D(D_2), .Q(out_32), .CLK(CLK_2), .EN(EN));
  \存储器阵列  \u_存储器阵列_1  (
    .in_6(A1), .in_7(A0), .in_4(D0), .in_1(D1), .in_2(D2), .in_3(D3), .CLK(CLK_5), .out_8(Q0), .out_9(Q1_2),
    .out_10(Q2_2), .out_11(Q3_2));

  // Notes on the sheet:
  //   交叉耦合的反相器
  //   复用器实现
  //   与门实现
endmodule

module \SR锁存器  (
  input  ReSet,
  input  Set,
  output Q,
  output Not_Q
);

  nor nor_1 (Q, ReSet, Not_Q);
  nor nor_2 (Not_Q, Q, Set);

  // Notes on the sheet:
  //   SR锁存器
endmodule

module \D锁存器  (
  input  CLK,
  input  D,
  output Q,
  output Not_Q
);

  wire and_1_out, and_2_out, not_1_out;

  not not_1 (not_1_out, D);
  and and_1 (and_1_out, CLK, not_1_out);
  and and_2 (and_2_out, CLK, D);
  \SR锁存器  \sr锁存器_1  (.ReSet(and_1_out), .Set(and_2_out), .Q(Q), .Not_Q(Not_Q));
endmodule

module \D触发器  (
  input  in_1,
  input  D,
  output out_3,
  output out_4
);

  wire \d锁存器_1_q , not_1_out;

  not not_1 (not_1_out, in_1);
  \D锁存器  \d锁存器_1  (.D(D), .Q(\d锁存器_1_q ), .CLK(not_1_out));  // open: Not_Q
  \D锁存器  \d锁存器_2  (.D(\d锁存器_1_q ), .Q(out_3), .Not_Q(out_4), .CLK(in_1));
endmodule

module \寄存器  (
  input  in_1,
  input  D3,
  input  D2,
  input  D1,
  input  D0,
  output Q3,
  output Q2,
  output Q1,
  output Q0
);

  \D触发器  \d触发器_1  (.D(D3), .out_3(Q3), .in_1(in_1));  // open: out_4
  \D触发器  \d触发器_2  (.D(D2), .out_3(Q2), .in_1(in_1));  // open: out_4
  \D触发器  \d触发器_3  (.D(D1), .out_3(Q1), .in_1(in_1));  // open: out_4
  \D触发器  \d触发器_4  (.D(D0), .out_3(Q0), .in_1(in_1));  // open: out_4
endmodule

// 带使能端的触发器
module \带使能端的D触发器  (
  input  CLK,
  input  EN,
  input  D,
  output Q
);

  wire \n2_1复用器_1_out_4 ;

  \_2_1复用器  \u_2_1复用器_1  (.in_2(D), .in_3(Q), .out_4(\n2_1复用器_1_out_4 ), .EN(EN));
  \D触发器  \d触发器_1  (.D(\n2_1复用器_1_out_4 ), .out_3(Q), .in_1(CLK));  // open: out_4
endmodule

module \_2_1复用器  (
  input  EN,
  input  in_2,
  input  in_3,
  output out_4
);

  wire and_1_out, and_2_out, not_1_out;

  and and_1 (and_1_out, EN, in_2);
  not not_1 (not_1_out, EN);
  and and_2 (and_2_out, not_1_out, in_3);
  or or_1 (out_4, and_1_out, and_2_out);
endmodule

// 复位功能的触发器
module \带复位功能的触发器  (
  input  CLK,
  input  D,
  input  in_3,
  output Q
);

  wire and_1_out, not_1_out;

  not not_1 (not_1_out, in_3);
  and and_1 (and_1_out, D, not_1_out);
  \D触发器  \d触发器_1  (.D(and_1_out), .out_3(Q), .in_1(CLK));  // open: out_4
endmodule

// 带使能端的触发器
module \带使能端的复用器2  (
  input  CLK,
  input  EN,
  input  D,
  output Q
);

  wire and_1_out;

  and and_1 (and_1_out, CLK, EN);
  \D触发器  \d触发器_1  (.D(D), .out_3(Q), .in_1(and_1_out));  // open: out_4
endmodule

module \存储器阵列  (
  input  in_1,
  input  in_2,
  input  in_3,
  input  in_4,
  input  CLK,
  input  in_6,
  input  in_7,
  output out_8,
  output out_9,
  output out_10,
  output out_11
);

  wire \带使能端的d触发器_1_q , \带使能端的d触发器_2_q , \带使能端的d触发器_3_q , \带使能端的d触发器_4_q , \带使能端的d触发器_5_q , \带使能端的d触发器_6_q ,
       \带使能端的d触发器_7_q , \带使能端的d触发器_8_q , \带使能端的d触发器_9_q , \带使能端的d触发器_10_q , \带使能端的d触发器_11_q ,
       \带使能端的d触发器_12_q , \带使能端的d触发器_13_q , \带使能端的d触发器_14_q , \带使能端的d触发器_15_q , \带使能端的d触发器_16_q ,
       \译码器_1_out_3 , \译码器_1_out_4 , \译码器_1_out_5 , \译码器_1_out_6 ;

  \译码器  \u_译码器_1  (
    .in_2(in_7), .out_3(\译码器_1_out_3 ), .out_4(\译码器_1_out_4 ), .out_5(\译码器_1_out_5 ), .out_6(\译码器_1_out_6 ),
    .in_1(in_6));
  \带使能端的D触发器  \u_带使能端的d触发器_1  (.D(in_4), .Q(\带使能端的d触发器_1_q ), .EN(\译码器_1_out_3 ), .CLK(CLK));
  assign out_8 = \译码器_1_out_3  ? \带使能端的d触发器_1_q  : 1'bz;  // Controlled_Buffer controlled_buffer_1
  assign out_8 = \译码器_1_out_4  ? \带使能端的d触发器_2_q  : 1'bz;  // Controlled_Buffer controlled_buffer_2
  \带使能端的D触发器  \u_带使能端的d触发器_2  (.D(in_4), .Q(\带使能端的d触发器_2_q ), .EN(\译码器_1_out_4 ), .CLK(CLK));
  \带使能端的D触发器  \u_带使能端的d触发器_3  (.D(in_4), .Q(\带使能端的d触发器_3_q ), .EN(\译码器_1_out_5 ), .CLK(CLK));
  assign out_8 = \译码器_1_out_5  ? \带使能端的d触发器_3_q  : 1'bz;  // Controlled_Buffer controlled_buffer_3
  \带使能端的D触发器  \u_带使能端的d触发器_4  (.D(in_4), .Q(\带使能端的d触发器_4_q ), .EN(\译码器_1_out_6 ), .CLK(CLK));
  assign out_8 = \译码器_1_out_6  ? \带使能端的d触发器_4_q  : 1'bz;  // Controlled_Buffer controlled_buffer_4
  \带使能端的D触发器  \u_带使能端的d触发器_5  (.D(in_1), .Q(\带使能端的d触发器_5_q ), .EN(\译码器_1_out_3 ), .CLK(CLK));
  assign out_9 = \译码器_1_out_3  ? \带使能端的d触发器_5_q  : 1'bz;  // Controlled_Buffer controlled_buffer_5
  \带使能端的D触发器  \u_带使能端的d触发器_6  (.D(in_1), .Q(\带使能端的d触发器_6_q ), .EN(\译码器_1_out_4 ), .CLK(CLK));
  assign out_9 = \译码器_1_out_4  ? \带使能端的d触发器_6_q  : 1'bz;  // Controlled_Buffer controlled_buffer_6
  assign out_9 = \译码器_1_out_5  ? \带使能端的d触发器_7_q  : 1'bz;  // Controlled_Buffer controlled_buffer_7
  \带使能端的D触发器  \u_带使能端的d触发器_7  (.D(in_1), .Q(\带使能端的d触发器_7_q ), .EN(\译码器_1_out_5 ), .CLK(CLK));
  assign out_9 = \译码器_1_out_6  ? \带使能端的d触发器_8_q  : 1'bz;  // Controlled_Buffer controlled_buffer_8
  \带使能端的D触发器  \u_带使能端的d触发器_8  (.D(in_1), .Q(\带使能端的d触发器_8_q ), .EN(\译码器_1_out_6 ), .CLK(CLK));
  assign out_10 = \译码器_1_out_3  ? \带使能端的d触发器_9_q  : 1'bz;  // Controlled_Buffer controlled_buffer_9
  \带使能端的D触发器  \u_带使能端的d触发器_9  (.D(in_2), .Q(\带使能端的d触发器_9_q ), .EN(\译码器_1_out_3 ), .CLK(CLK));
  \带使能端的D触发器  \u_带使能端的d触发器_10  (.D(in_2), .Q(\带使能端的d触发器_10_q ), .EN(\译码器_1_out_4 ), .CLK(CLK));
  assign out_10 = \译码器_1_out_4  ? \带使能端的d触发器_10_q  : 1'bz;  // Controlled_Buffer controlled_buffer_10
  \带使能端的D触发器  \u_带使能端的d触发器_11  (.D(in_2), .Q(\带使能端的d触发器_11_q ), .EN(\译码器_1_out_5 ), .CLK(CLK));
  assign out_10 = \译码器_1_out_5  ? \带使能端的d触发器_11_q  : 1'bz;  // Controlled_Buffer controlled_buffer_11
  assign out_10 = \译码器_1_out_6  ? \带使能端的d触发器_12_q  : 1'bz;  // Controlled_Buffer controlled_buffer_12
  \带使能端的D触发器  \u_带使能端的d触发器_12  (.D(in_2), .Q(\带使能端的d触发器_12_q ), .EN(\译码器_1_out_6 ), .CLK(CLK));
  assign out_11 = \译码器_1_out_3  ? \带使能端的d触发器_13_q  : 1'bz;  // Controlled_Buffer controlled_buffer_13
  \带使能端的D触发器  \u_带使能端的d触发器_13  (.D(in_3), .Q(\带使能端的d触发器_13_q ), .EN(\译码器_1_out_3 ), .CLK(CLK));
  \带使能端的D触发器  \u_带使能端的d触发器_14  (.D(in_3), .Q(\带使能端的d触发器_14_q ), .EN(\译码器_1_out_4 ), .CLK(CLK));
  assign out_11 = \译码器_1_out_4  ? \带使能端的d触发器_14_q  : 1'bz;  // Controlled_Buffer controlled_buffer_14
  \带使能端的D触发器  \u_带使能端的d触发器_15  (.D(in_3), .Q(\带使能端的d触发器_15_q ), .EN(\译码器_1_out_5 ), .CLK(CLK));
  assign out_11 = \译码器_1_out_5  ? \带使能端的d触发器_15_q  : 1'bz;  // Controlled_Buffer controlled_buffer_15
  \带使能端的D触发器  \u_带使能端的d触发器_16  (.D(in_3), .Q(\带使能端的d触发器_16_q ), .EN(\译码器_1_out_6 ), .CLK(CLK));
  assign out_11 = \译码器_1_out_6  ? \带使能端的d触发器_16_q  : 1'bz;  // Controlled_Buffer controlled_buffer_16
endmodule

module \译码器  (
  input  in_1,
  input  in_2,
  output out_3,
  output out_4,
  output out_5,
  output out_6
);

  wire not_1_out, not_2_out, not_3_out, not_4_out;

  not not_1 (not_1_out, in_2);
  not not_2 (not_2_out, in_1);
  not not_3 (not_3_out, in_1);
  not not_4 (not_4_out, in_2);
  and and_1 (out_3, in_2, in_1);
  and and_2 (out_4, not_1_out, in_1);
  and and_3 (out_5, not_2_out, in_2);
  and and_4 (out_6, not_3_out, not_4_out);
endmodule

module \移位寄存器  (
);

  wire button_1_out, clock_1_out, \d触发器_1_out_3 , \d触发器_2_out_3 , \d触发器_3_out_3 , \d触发器_4_out_3 ,
       \d触发器_5_out_3 , \d触发器_6_out_3 , \d触发器_7_out_3 , \d触发器_8_out_3 , \d触发器_9_out_3 , \d触发器_10_out_3 ,
       \d触发器_11_out_3 ;

  Button button_1 (.out(button_1_out));
  \D触发器  \d触发器_1  (.D(button_1_out), .out_3(\d触发器_1_out_3 ), .in_1(clock_1_out));  // open: out_4
  LED led_1 (.in(\d触发器_1_out_3 ));
  \D触发器  \d触发器_2  (.D(\d触发器_1_out_3 ), .out_3(\d触发器_2_out_3 ), .in_1(clock_1_out));  // open: out_4
  LED led_2 (.in(\d触发器_2_out_3 ));
  \D触发器  \d触发器_3  (.D(\d触发器_2_out_3 ), .out_3(\d触发器_3_out_3 ), .in_1(clock_1_out));  // open: out_4
  LED led_3 (.in(\d触发器_3_out_3 ));
  \D触发器  \d触发器_4  (.D(\d触发器_3_out_3 ), .out_3(\d触发器_4_out_3 ), .in_1(clock_1_out));  // open: out_4
  LED led_4 (.in(\d触发器_4_out_3 ));
  \D触发器  \d触发器_5  (.D(\d触发器_4_out_3 ), .out_3(\d触发器_5_out_3 ), .in_1(clock_1_out));  // open: out_4
  LED led_5 (.in(\d触发器_5_out_3 ));
  \D触发器  \d触发器_6  (.D(\d触发器_5_out_3 ), .out_3(\d触发器_6_out_3 ), .in_1(clock_1_out));  // open: out_4
  LED led_6 (.in(\d触发器_6_out_3 ));
  \D触发器  \d触发器_7  (.D(\d触发器_6_out_3 ), .out_3(\d触发器_7_out_3 ), .in_1(clock_1_out));  // open: out_4
  LED led_7 (.in(\d触发器_7_out_3 ));
  \D触发器  \d触发器_8  (.D(\d触发器_7_out_3 ), .out_3(\d触发器_8_out_3 ), .in_1(clock_1_out));  // open: out_4
  LED led_8 (.in(\d触发器_8_out_3 ));
  \D触发器  \d触发器_9  (.D(\d触发器_8_out_3 ), .out_3(\d触发器_9_out_3 ), .in_1(clock_1_out));  // open: out_4
  LED led_9 (.in(\d触发器_9_out_3 ));
  \D触发器  \d触发器_10  (.D(\d触发器_9_out_3 ), .out_3(\d触发器_10_out_3 ), .in_1(clock_1_out));  // open: out_4
  LED led_10 (.in(\d触发器_10_out_3 ));
  \D触发器  \d触发器_11  (.D(\d触发器_10_out_3 ), .out_3(\d触发器_11_out_3 ), .in_1(clock_1_out));  // open: out_4
  LED led_11 (.in(\d触发器_11_out_3 ));
  Clock clock_1 (.out(clock_1_out));
endmodule
